// Logisim project prog_calculator.circ as structural Verilog: 3 circuits, main circuit alu
module alu (
  input  [7:0] a,
  input  [7:0] b,
  input  [3:0] alu_op,
  input  [3:0] imm4,
  output [7:0] y
);

  wire or_2_out;
  wire [7:0] adder_1_out, adder_2_out, and_1_out, bit_extender_1_out, bit_extender_2_out, multiplexer_1_out,
       multiplexer_2_out, multiplier_1_out, not_1_out, or_1_out, shifter_1_out, shifter_2_out,
       subtractor_1_out;

  assign bit_extender_1_out = {{4{1'b0}}, imm4};  // Bit_Extender bit_extender_1
  Adder adder_1 (.a(a), .b(b), .out(adder_1_out));  // open: cin, cout
  Subtractor subtractor_1 (.a(a), .b(b), .out(subtractor_1_out));  // open: bin, bout
  assign and_1_out = a & b;  // AND_Gate and_1, 8 bits wide
  assign or_1_out = a | b;  // OR_Gate or_1, 8 bits wide
  Shifter shifter_1 (.in(a), .\dist (b[2:0]), .out(shifter_1_out));
  or or_2 (or_2_out, b[3], b[4], b[5], b[6], b[7]);
  Shifter #(.shift("lr")) shifter_2 (.in(a), .\dist (b[2:0]), .out(shifter_2_out));
  Multiplier #(.mode("twosComplement")) multiplier_1 (.a(a), .b(b), .out(multiplier_1_out));  // open: cin, cout
  assign bit_extender_2_out = {{4{imm4[3]}}, imm4};  // Bit_Extender bit_extender_2
  assign not_1_out = ~a;  // NOT_Gate not_1, 8 bits wide
  Multiplexer #(.width(8)) multiplexer_1 (
    .in0(shifter_1_out), .in1({8{1'b0}}), .out(multiplexer_1_out), .sel(or_2_out));
  Multiplexer #(.width(8)) multiplexer_2 (
    .in0(shifter_2_out), .in1({8{1'b0}}), .out(multiplexer_2_out), .sel(or_2_out));
  Adder adder_2 (.a(a), .b(bit_extender_2_out), .out(adder_2_out));  // open: cin, cout
  Multiplexer #(.select(4), .width(8)) multiplexer_3 (
    .in0(adder_1_out), .in1(subtractor_1_out), .in2(and_1_out), .in3(or_1_out), .in4(not_1_out),
    .in5(multiplexer_1_out), .in6(multiplexer_2_out), .in7(bit_extender_1_out), .in8(adder_2_out),
    .in9(bit_extender_2_out), .in10(multiplier_1_out), .out(y), .sel(alu_op));  // open: in11, in12, in13, in14, in15
endmodule

module regfile (
  input  [2:0] raddrb,
  input  [7:0] din,
  input  clk,
  input  [2:0] raddra,
  input  [2:0] waddr,
  output [7:0] doutb,
  output [7:0] douta
);

  wire decoder_1_out0, decoder_1_out1, decoder_1_out2, decoder_1_out3, decoder_1_out4, decoder_1_out5,
       decoder_1_out6, decoder_1_out7;
  wire [7:0] r0_q, r1_q, r2_q, r3_q, r4_q, r5_q, r6_q, r7_q;

  Decoder #(.enable("false"), .select(3)) decoder_1 (
    .out0(decoder_1_out0), .out1(decoder_1_out1), .out2(decoder_1_out2), .out3(decoder_1_out3),
    .out4(decoder_1_out4), .out5(decoder_1_out5), .out6(decoder_1_out6), .out7(decoder_1_out7), .sel(waddr));
  Register r0 (.D(din), .en(decoder_1_out0), .clk(clk), .Q(r0_q));  // open: clr
  Register r1 (.D(din), .en(decoder_1_out1), .clk(clk), .Q(r1_q));  // open: clr
  Register r2 (.D(din), .en(decoder_1_out2), .clk(clk), .Q(r2_q));  // open: clr
  Register r3 (.D(din), .en(decoder_1_out3), .clk(clk), .Q(r3_q));  // open: clr
  Register r4 (.D(din), .en(decoder_1_out4), .clk(clk), .Q(r4_q));  // open: clr
  Register r5 (.D(din), .en(decoder_1_out5), .clk(clk), .Q(r5_q));  // open: clr
  Register r6 (.D(din), .en(decoder_1_out6), .clk(clk), .Q(r6_q));  // open: clr
  Register r7 (.D(din), .en(decoder_1_out7), .clk(clk), .Q(r7_q));  // open: clr
  Multiplexer #(.select(3), .width(8)) multiplexer_1 (
    .in0(r0_q), .in1(r1_q), .in2(r2_q), .in3(r3_q), .in4(r4_q), .in5(r5_q), .in6(r6_q), .in7(r7_q),
    .out(doutb), .sel(raddrb));
  Multiplexer #(.select(3), .width(8)) multiplexer_2 (
    .in0(r0_q), .in1(r1_q), .in2(r2_q), .in3(r3_q), .in4(r4_q), .in5(r5_q), .in6(r6_q), .in7(r7_q),
    .out(douta), .sel(raddra));
endmodule

module calculator (
  input  clk,
  input  [2:0] ra,
  input  [3:0] op,
  input  [2:0] rb,
  input  [3:0] imm4,
  input  [2:0] rw,
  output [7:0] y
);

  wire [7:0] regfile_1_douta, regfile_1_doutb;

  regfile regfile_1 (
    .raddrb(rb), .din(y), .clk(clk), .raddra(ra), .waddr(rw), .doutb(regfile_1_doutb), .douta(regfile_1_douta));
  alu alu_1 (.a(regfile_1_douta), .b(regfile_1_doutb), .alu_op(op), .imm4(imm4), .y(y));
endmodule
