// Logisim project client_server_system.circ as structural Verilog
module client_comb (
  input  p1,
  input  p0,
  input  ack,
  output n1,
  output n0,
  output req,
  output process_ack
);

  wire and_2_out, and_3_out, not_1_out, not_2_out, not_3_out;

  not not_1 (not_1_out, p1);
  not not_2 (not_2_out, p0);
  not not_3 (not_3_out, ack);
  and and_1 (n1, p0, ack);
  and and_2 (and_2_out, not_1_out, not_2_out);
  and and_3 (and_3_out, not_1_out, not_3_out);
  and and_4 (req, not_1_out, not_2_out);
  or or_1 (n0, and_2_out, and_3_out);

  assign process_ack = p1;
endmodule

module client_state_reg (
  input  [1:0] next_state,
  input  clk,
  input  rst,
  output [1:0] state
);

  Register #(.width(2)) register_1 (.D(next_state), .en(1'b1), .clk(clk), .Q(state), .clr(rst));
endmodule

module client (
  input  clk,
  input  reset,
  input  ack,
  output req,
  output process_ack
);

  wire [1:0] client_comb_1_n0, client_state_reg_1_state;

  client_state_reg client_state_reg_1 (
    .next_state(client_comb_1_n0), .clk(clk), .rst(reset), .state(client_state_reg_1_state));
  client_comb client_comb_1 (
    .p1(client_state_reg_1_state[1]), .p0(client_state_reg_1_state[0]), .ack(ack), .n1(client_comb_1_n0[1]),
    .n0(client_comb_1_n0[0]), .req(req), .process_ack(process_ack));
endmodule
