// Logisim project hardware_divider.circ as structural Verilog
module load_register8 (
  input  [7:0] d,
  input  en,
  input  clk,
  input  rst,
  output [7:0] q
);

  Register register_1 (.D(d), .en(en), .clk(clk), .Q(q), .clr(rst));
endmodule

module div_datapath (
  input  en_quotient,
  input  [1:0] sel_quotient,
  input  en_i,
  input  sel_i,
  input  [3:0] dividend_in,
  input  en_remainder,
  input  [1:0] sel_remainder,
  input  [3:0] divisor_in,
  input  en_divisor,
  input  sel_divisor,
  output [7:0] quotient_out
);

  wire [7:0] adder_1_out, divisor_q, i_q, multiplexer_1_out, multiplexer_2_out, multiplexer_3_out,
       multiplexer_4_out, remainder_q, shifter_1_out, subtractor_1_out, subtractor_2_out;

  Subtractor subtractor_1 (.a(remainder_q), .b(divisor_q), .out(subtractor_1_out));  // open: bin, bout
  Adder adder_1 (.a(remainder_q), .b(divisor_q), .out(adder_1_out));  // open: cin, cout
  Shifter #(.shift("lr")) shifter_1 (.in(divisor_q), .\dist (3'b001), .out(shifter_1_out));
  Subtractor subtractor_2 (.a(i_q), .b(8'h1), .out(subtractor_2_out));  // open: bin, bout
  Multiplexer #(.select(2), .width(8)) multiplexer_1 (
    .in0({8{1'b0}}), .in1({quotient_out[6:0], 1'b0}), .in2({quotient_out[6:0], 1'b1}),
    .out(multiplexer_1_out), .sel(sel_quotient));  // open: in3
  Multiplexer #(.width(8)) multiplexer_2 (.in0(8'h4), .out(multiplexer_2_out), .sel(sel_i));  // open: in1
  Multiplexer #(.select(2), .width(8)) multiplexer_3 (
    .in0({4'b0000, dividend_in}), .in1(subtractor_1_out), .in2(adder_1_out), .out(multiplexer_3_out),
    .sel(sel_remainder));  // open: in3
  Multiplexer #(.width(8)) multiplexer_4 (
    .in0({divisor_in, 4'b0000}), .out(multiplexer_4_out), .sel(sel_divisor));  // open: in1
  load_register8 quotient (.d(multiplexer_1_out), .en(en_quotient), .q(quotient_out));  // open: clk, rst
  load_register8 i (.d(multiplexer_2_out), .en(en_i), .q(i_q));  // open: clk, rst
  load_register8 remainder (.d(multiplexer_3_out), .en(en_remainder), .q(remainder_q));  // open: clk, rst
  load_register8 divisor (.d(multiplexer_4_out), .en(en_divisor), .q(divisor_q));  // open: clk, rst
endmodule
